# Fritzing sketch IbS2026 (saved by Fritzing 1.0.7)
breadboards: 1

parts:
  CPU1 = NodeMCU WROOM ESP 32
  E-Ink_Display = Waveshare e-Paper HAT [package=THT]
  Power_Supply = YwRobot Breadboard Power Supply [part_number=545043]
  DHT11 = Humidity and Temperature Sensor DHT11
  L293D = L293D [package=THT]
  DC_Motor = DC Motor [voltage_(max)=6V voltage_(min)=3V]
  Photocell = Photocell (LDR) [power=0.25W dark_resistance_@0.01lx=300kΩ light_resistance_@100lx=400Ω luminance=10lx package=THT]
  Alarm_stop = Momentary Switch [package=ksa_sealed_tac_switch]
  Servo_Motor = Basic Servo
  Potentiometer = Trimmer Potentiometer [maximum_resistance=10kΩ knob_status=50% power=0.5W package=THT]
  Buzzer = Piezo Speaker
  part = Resistor [tolerance=±1% power=0.25W resistance=1k package=THT]

nets:
  N1: CPU1.pin_6, DHT11.Data-signal
  N2: CPU1.pin_7, Photocell.pin_1, part.Pin_1
  N3: CPU1.pin_9, CPU1.pin_25, E-Ink_Display.pin_5, L293D.In_3
  N4: CPU1.pin_10, L293D.In_4
  N5: CPU1.pin_11, L293D.Enable_2
  N6: CPU1.pin_13, Potentiometer.leg1, Potentiometer.leg2
  N7: CPU1.pin_14, Servo_Motor.pulse
  N8: CPU1.pin_17, E-Ink_Display.pin_8
  N9: CPU1.pin_18, E-Ink_Display.pin_7
  N10: CPU1.pin_21, E-Ink_Display.pin_1
  N11: CPU1.pin_22, E-Ink_Display.pin_2
  N12: CPU1.pin_23, E-Ink_Display.pin_3
  N13: CPU1.pin_24, E-Ink_Display.pin_4
  N14: CPU1.pin_31, E-Ink_Display.pin_6
  N15: Power_Supply.VCC#5, Power_Supply.VCC#6, Servo_Motor.vcc
  N16: Power_Supply.VCC#9, Power_Supply.VCC#10, DHT11.Vcc, L293D.+Vmotor, L293D.+V, Photocell.pin_0
  N17: Power_Supply.GND#11, Power_Supply.GND#12, Servo_Motor.gnd
  N18: Power_Supply.GND#13, Power_Supply.GND#14, DHT11.GND, L293D.0V, Alarm_stop.3, Alarm_stop.4, Buzzer.pin1, part.Pin_0
  N19: L293D.Out_3_(_Controlled_by_Enable_2_), DC_Motor.pin_1
  N20: L293D.Out_4_(_Controlled_by_Enable_2_), DC_Motor.pin_2
  N21: Alarm_stop.1, Alarm_stop.2
  N22: Potentiometer.wiper, Buzzer.pin2

custom parts:
  NodeMCU WROOM ESP 32: 30 pol Development Kit
  Waveshare e-Paper HAT: .This is a universal driver board for e-Paper raw panels, can be used to drive various SPI interface e-Paper from Waveshare.
  YwRobot Breadboard Power Supply: The YwRobot Breadboard Power Supply (MB-V2) has two power rails; they can be 5V or 3V3. Power to the module can be provided through the female USB socket or through the A10 (female) 2.1mm power jack.
  Humidity and Temperature Sensor DHT11: Digital relative humidity & temperature sensor DHT11
